// Logisim project CPU.circ as structural Verilog: 10 circuits, main circuit main
module main (
  input  reset
);

  wire AI, AO, BI, CE, CF, clk, CO, comp_clock_out, EO, FI, HLT, II, IO, J, MI, OI, RI, RO, SU, t_ff_1_qn, ZF;
  wire [3:0] instruction_reg_1_ins_reg_out, mem_addr_reg_1_mem_reg_addr_out, op_reg_1_hundreds,
       op_reg_1_ones, op_reg_1_tens;
  wire [7:0] a_register_1_a_reg_out, b_register_1_b_reg_out, ram_module_1_ram_out;

  Clock #(.highDuration(2), .lowDuration(2)) comp_clock (.out(comp_clock_out));
  T_Flip_Flop t_ff_1 (.T(HLT), .clk(clk), .Qn(t_ff_1_qn), .reset(reset));  // open: Q, preset
  and and_1 (clk, comp_clock_out, t_ff_1_qn);
  Control_circuitry control_circuitry_1 (
    .ZF(reset), .reset(ZF), .CF(CF), .CLK(clk), .Instruction(instruction_reg_1_ins_reg_out), .FI(FI),
    .BI(BI), .SU(SU), .EO(EO), .AO(AO), .AI(AI), .CE(CE), .J(J), .CO(CO), .IO(IO), .II(II), .RO(RO), .RI(RI),
    .OI(OI), .MI(MI), .HLT(HLT));
  Mem_addr_reg mem_addr_reg_1 (
    .BUS_in(ram_module_1_ram_out), .MI(MI), .clk(clk), .reset(reset),
    .mem_reg_addr_out(mem_addr_reg_1_mem_reg_addr_out));
  RAM_module ram_module_1 (
    .mem_addr_in(mem_addr_reg_1_mem_reg_addr_out), .RI(RI), .clk(clk), .RAM_in(ram_module_1_ram_out),
    .RO(RO), .RAM_out(ram_module_1_ram_out));
  Instruction_reg instruction_reg_1 (
    .BUS_in(ram_module_1_ram_out), .IO(IO), .II(II), .clk(clk), .reset(reset),
    .BUS_out(ram_module_1_ram_out), .ins_reg_out(instruction_reg_1_ins_reg_out));
  LedBar ledbar_1 (
    .led0(ram_module_1_ram_out[7]), .led1(ram_module_1_ram_out[6]), .led2(ram_module_1_ram_out[5]),
    .led3(ram_module_1_ram_out[4]), .led4(ram_module_1_ram_out[3]), .led5(ram_module_1_ram_out[2]),
    .led6(ram_module_1_ram_out[1]), .led7(ram_module_1_ram_out[0]));
  Program_counter program_counter_1 (
    .reset(reset), .J(J), .CE(CE), .Clk(clk), .CO(CO), .BUS_in(ram_module_1_ram_out),
    .BUS_out(ram_module_1_ram_out));
  LedBar ledbar_2 (
    .led0(a_register_1_a_reg_out[7]), .led1(a_register_1_a_reg_out[6]), .led2(a_register_1_a_reg_out[5]),
    .led3(a_register_1_a_reg_out[4]), .led4(a_register_1_a_reg_out[3]), .led5(a_register_1_a_reg_out[2]),
    .led6(a_register_1_a_reg_out[1]), .led7(a_register_1_a_reg_out[0]));
  A_register a_register_1 (
    .BUS_in(ram_module_1_ram_out), .AI(AI), .AO(AO), .Clk(clk), .reset(reset),
    .A_reg_out(a_register_1_a_reg_out), .BUS_out(ram_module_1_ram_out));
  ALU alu_1 (
    .SU(SU), .A(a_register_1_a_reg_out), .B(b_register_1_b_reg_out), .EO(EO), .FI(FI), .CLK(clk),
    .Reset(reset), .ALU_out(ram_module_1_ram_out), .ZF(ZF), .CF(CF));
  B_register b_register_1 (
    .BUS_in(ram_module_1_ram_out), .BI(BI), .Clk(clk), .reset(reset), .B_reg_out(b_register_1_b_reg_out));
  Op_reg op_reg_1 (
    .BUS_in(ram_module_1_ram_out), .OI(OI), .clk(clk), .reset(reset), .hundreds(op_reg_1_hundreds),
    .tens(op_reg_1_tens), .ones(op_reg_1_ones));
  _7_Segment_Display u_7_segment_display_1 ();  // open: g, f, a, b, e, d, c, dp
  // BCD_to_7_Segment_decoder bcd_to_7_segment_decoder_1: pin names not known; wires that end beside it: op_reg_1_hundreds
  _7_Segment_Display u_7_segment_display_2 ();  // open: g, f, a, b, e, d, c, dp
  _7_Segment_Display u_7_segment_display_3 ();  // open: g, f, a, b, e, d, c, dp
  // BCD_to_7_Segment_decoder bcd_to_7_segment_decoder_2: pin names not known; wires that end beside it: op_reg_1_tens
  // BCD_to_7_Segment_decoder bcd_to_7_segment_decoder_3: pin names not known; wires that end beside it: op_reg_1_ones
endmodule

module ALU (
  input  SU,
  input  [7:0] A,
  input  [7:0] B,
  input  EO,
  input  FI,
  input  CLK,
  input  Reset,
  output [7:0] ALU_out,
  output ZF,
  output CF
);

  wire adder_1_cout, adder_1_out, adder_2_cout, adder_2_out, adder_3_cout, adder_3_out, adder_4_cout,
       adder_4_out, adder_5_cout, adder_5_out, adder_6_cout, adder_6_out, adder_7_cout, adder_7_out,
       adder_8_out, xor_1_out, xor_2_out, xor_3_out, xor_4_out, xor_5_out, xor_6_out, xor_7_out, xor_8_out;
  wire [1:0] nor_1_out;

  xor xor_1 (xor_1_out, B[0], SU);
  xor xor_2 (xor_2_out, B[1], SU);
  xor xor_3 (xor_3_out, B[2], SU);
  xor xor_4 (xor_4_out, B[3], SU);
  xor xor_5 (xor_5_out, B[4], SU);
  xor xor_6 (xor_6_out, B[5], SU);
  xor xor_7 (xor_7_out, B[6], SU);
  xor xor_8 (xor_8_out, B[7], SU);
  Adder #(.width(1)) adder_1 (.a(A[0]), .b(xor_1_out), .out(adder_1_out), .cin(SU), .cout(adder_1_cout));
  Adder #(.width(1)) adder_2 (.a(A[1]), .b(xor_2_out), .out(adder_2_out), .cin(adder_1_cout), .cout(adder_2_cout));
  Adder #(.width(1)) adder_3 (.a(A[2]), .b(xor_3_out), .out(adder_3_out), .cin(adder_2_cout), .cout(adder_3_cout));
  Adder #(.width(1)) adder_4 (.a(A[3]), .b(xor_4_out), .out(adder_4_out), .cin(adder_3_cout), .cout(adder_4_cout));
  Adder #(.width(1)) adder_5 (.a(A[4]), .b(xor_5_out), .out(adder_5_out), .cin(adder_4_cout), .cout(adder_5_cout));
  Adder #(.width(1)) adder_6 (.a(A[5]), .b(xor_6_out), .out(adder_6_out), .cin(adder_5_cout), .cout(adder_6_cout));
  Adder #(.width(1)) adder_7 (.a(A[6]), .b(xor_7_out), .out(adder_7_out), .cin(adder_6_cout), .cout(adder_7_cout));
  Adder #(.width(1)) adder_8 (.a(A[7]), .b(xor_8_out), .out(adder_8_out), .cin(adder_7_cout), .cout(nor_1_out[1]));
  nor nor_1 (nor_1_out[0], adder_1_out, adder_2_out, adder_3_out, adder_4_out, adder_5_out, adder_6_out, adder_7_out, adder_8_out);
  assign ALU_out[0] = EO ? adder_1_out : 1'bz;  // Controlled_Buffer controlled_buffer_1
  assign ALU_out[1] = EO ? adder_2_out : 1'bz;  // Controlled_Buffer controlled_buffer_2
  assign ALU_out[2] = EO ? adder_3_out : 1'bz;  // Controlled_Buffer controlled_buffer_3
  assign ALU_out[3] = EO ? adder_4_out : 1'bz;  // Controlled_Buffer controlled_buffer_4
  Register #(.width(2)) register_1 (.D(nor_1_out), .en(FI), .clk(CLK), .Q({CF, ZF}), .clr(Reset));
  assign ALU_out[4] = EO ? adder_5_out : 1'bz;  // Controlled_Buffer controlled_buffer_5
  assign ALU_out[5] = EO ? adder_6_out : 1'bz;  // Controlled_Buffer controlled_buffer_6
  assign ALU_out[6] = EO ? adder_7_out : 1'bz;  // Controlled_Buffer controlled_buffer_7
  assign ALU_out[7] = EO ? adder_8_out : 1'bz;  // Controlled_Buffer controlled_buffer_8
endmodule

// BUS_out
module A_register (
  input  [7:0] BUS_in,
  input  AI,
  input  AO,
  input  Clk,
  input  reset,
  output [7:0] A_reg_out,
  output [7:0] BUS_out
);

  Register register_1 (.D(BUS_in), .en(AI), .clk(Clk), .Q(A_reg_out), .clr(reset));
  assign BUS_out = AO ? A_reg_out : 8'bz;  // Controlled_Buffer controlled_buffer_1
endmodule

module B_register (
  input  [7:0] BUS_in,
  input  BI,
  input  Clk,
  input  reset,
  output [7:0] B_reg_out
);

  Register register_1 (.D(BUS_in), .en(BI), .clk(Clk), .Q(B_reg_out), .clr(reset));
endmodule

module Mem_addr_reg (
  input  [7:0] BUS_in,
  input  MI,
  input  clk,
  input  reset,
  output [3:0] mem_reg_addr_out
);

  Register #(.width(4)) register_1 (.D(BUS_in[3:0]), .en(MI), .clk(clk), .Q(mem_reg_addr_out), .clr(reset));
endmodule

module RAM_module (
  input  [3:0] mem_addr_in,
  input  RI,
  input  clk,
  input  [7:0] RAM_in,
  input  RO,
  output [7:0] RAM_out
);

  wire [7:0] Programs_dout;

  RAM #(.addrWidth(4), .enables("line")) Programs (
    .addr(mem_addr_in), .we(RI), .clk(clk), .din(RAM_in), .dout(Programs_dout));
  assign RAM_out = RO ? Programs_dout : 8'bz;  // Controlled_Buffer controlled_buffer_1
endmodule

module Instruction_reg (
  input  [7:0] BUS_in,
  input  IO,
  input  II,
  input  clk,
  input  reset,
  output [7:0] BUS_out,
  output [3:0] ins_reg_out
);

  wire [3:0] register_1_q;
  wire [7:0] bit_extender_1_out;

  Register register_1 (.D(BUS_in), .en(II), .clk(clk), .Q({ins_reg_out, register_1_q}), .clr(reset));
  assign bit_extender_1_out = {{4{1'b0}}, register_1_q};  // Bit_Extender bit_extender_1
  assign BUS_out = IO ? bit_extender_1_out : 8'bz;  // Controlled_Buffer controlled_buffer_1
endmodule

module Program_counter (
  input  reset,
  input  J,
  input  CE,
  input  Clk,
  input  CO,
  input  [7:0] BUS_in,
  output [7:0] BUS_out
);

  wire [3:0] counter_1_q;

  Counter #(.max('hf), .width(4)) counter_1 (
    .clr(reset), .load(J), .up(1'b1), .count(CE), .clk(Clk), .D(BUS_in[3:0]), .Q(counter_1_q));  // open: carry
  assign BUS_out = CO ? {4'b0000, counter_1_q} : 8'bz;  // Controlled_Buffer controlled_buffer_1
endmodule

module Op_reg (
  input  [7:0] BUS_in,
  input  OI,
  input  clk,
  input  reset,
  output [3:0] hundreds,
  output [3:0] tens,
  output [3:0] ones
);

  wire [7:0] register_1_q;

  Register register_1 (.D(BUS_in), .en(OI), .clk(clk), .Q(register_1_q), .clr(reset));
  // Binary_to_BCD_converter #(.binvalue(8)) binary_to_bcd_converter_1: pin names not known; wires that end beside it: register_1_q, hundreds, tens, ones
endmodule

module Control_circuitry (
  input  ZF,
  input  reset,
  input  CF,
  input  CLK,
  input  [3:0] Instruction,
  output FI,
  output BI,
  output SU,
  output EO,
  output AO,
  output AI,
  output CE,
  output J,
  output CO,
  output IO,
  output II,
  output RO,
  output RI,
  output OI,
  output MI,
  output HLT
);

  wire decoder_1_out5, not_1_out, or_1_out;
  wire [2:0] counter_1_q;

  not not_1 (not_1_out, CLK);
  Counter #(.max('h7), .width(3)) counter_1 (
    .clr(or_1_out), .load(1'b0), .up(1'b1), .count(1'b1), .clk(not_1_out), .Q(counter_1_q));  // open: D, carry
  or or_1 (or_1_out, decoder_1_out5, reset);
  Decoder #(.select(3)) decoder_1 (
    .out5(decoder_1_out5), .sel(counter_1_q), .en(1'b1));  // open: out0, out1, out2, out3, out4, out6, out7
  ROM #(.addrWidth(9), .dataWidth(16)) Control (
    .addr({CF, ZF, Instruction, counter_1_q}),
    .data({HLT, MI, OI, RI, RO, II, IO, CO, J, CE, AI, AO, EO, SU, BI, FI}));

  // Notes on the sheet:
  //   contents of Control (hex, n*v repeats v):
  //   4100 c40 6*0 4100 c40 4200 820 4*0 4100 c40 4200 802 29 0 0 0 4100 c40 4200 802 2d 0 0 0 4100 c40
  //   4200 1010 4*0 4100 c40 220 5*0 4100 c40 280 5*0 4100 c40 6*0 4100 c40 6*0 4100 c40 6*0 4100 c40 6*0
  //   4100 c40 6*0 4100 c40 6*0 4100 c40 6*0 4100 c40 2010 5*0 4100 c40 8000 5*0 4100 c40 6*0 4100 c40
  //   4200 820 4*0 4100 c40 4200 802 29 0 0 0 4100 c40 4200 802 2d 0 0 0 4100 c40 4200 1010 4*0 4100 c40
  //   220 5*0 4100 c40 280 5*0 4100 c40 6*0 4100 c40 280 5*0 4100 c40 6*0 4100 c40 6*0 4100 c40 6*0 4100
  //   c40 6*0 4100 c40 6*0 4100 c40 2010 5*0 4100 c40 8000 5*0 4100 c40 6*0 4100 c40 4200 820 4*0 4100 c40
  //   4200 802 29 0 0 0 4100 c40 4200 802 2d 0 0 0 4100 c40 4200 1010 4*0 4100 c40 220 5*0 4100 c40 280
  //   5*0 4100 c40 280 5*0 4100 c40 6*0 4100 c40 6*0 4100 c40 6*0 4100 c40 6*0 4100 c40 6*0 4100 c40 6*0
  //   4100 c40 2010 5*0 4100 c40 8000 5*0 4100 c40 6*0 4100 c40 4200 820 4*0 4100 c40 4200 802 29 0 0 0
  //   4100 c40 4200 802 2d 0 0 0 4100 c40 4200 1010 4*0 4100 c40 220 5*0 4100 c40 280 5*0 4100 c40 280 5*0
  //   4100 c40 280 5*0 4100 c40 6*0 4100 c40 6*0 4100 c40 6*0 4100 c40 6*0 4100 c40 6*0 4100 c40 2010 5*0
  //   4100 c40 8000
endmodule
